// Logisim project parte1_cache.circ as structural Verilog: 3 circuits, main circuit XOR_manual
module XOR_manual (
  input  A,
  input  B,
  output S
);

  wire and_1_out, and_2_out, not_1_out, not_2_out;

  and and_1 (and_1_out, A, not_1_out);
  not not_1 (not_1_out, B);
  not not_2 (not_2_out, A);
  and and_2 (and_2_out, not_2_out, B);
  or or_1 (S, and_1_out, and_2_out);
endmodule

module Cache (
  input  T2,
  input  T1,
  input  T0,
  input  A2,
  input  A1,
  input  Reset,
  output Iguais,
  output ACERTO
);

  wire bcd_to_7_segment_decoder_1_p2, clock_1_out, or_1_out, reg_cache_1_valido_indice, xor_manual_1_s,
       xor_manual_2_s, xor_manual_3_s;
  wire [2:0] reg_cache_1_rotulo_guardado;
  wire [7:0] counter_1_q;

  Clock clock_1 (.out(clock_1_out));
  XOR_manual xor_manual_1 (.A(T2), .B(reg_cache_1_rotulo_guardado[0]), .S(xor_manual_1_s));
  XOR_manual xor_manual_2 (.A(T1), .B(reg_cache_1_rotulo_guardado[1]), .S(xor_manual_2_s));
  XOR_manual xor_manual_3 (.A(T0), .B(reg_cache_1_rotulo_guardado[2]), .S(xor_manual_3_s));
  or or_1 (or_1_out, xor_manual_1_s, xor_manual_2_s, xor_manual_3_s);
  not not_1 (Iguais, or_1_out);
  Reg_Cache reg_cache_1 (
    .ACERTO(ACERTO), .A2(A2), .A1(A1), .Clock(clock_1_out), .Reg_Rotulo({T2, T1, T0}), .Reset(Reset),
    .Rotulo_Guardado(reg_cache_1_rotulo_guardado), .Valido_Indice(reg_cache_1_valido_indice));
  and and_1 (ACERTO, Iguais, reg_cache_1_valido_indice);
  Counter counter_1 (.clr(Reset), .count(ACERTO), .clk(clock_1_out), .Q(counter_1_q));  // open: load, up, D, carry
  // BCD_to_7_Segment_decoder bcd_to_7_segment_decoder_1: pin names not known; wires that end beside it: counter_1_q, bcd_to_7_segment_decoder_1_p2, bcd_to_7_segment_decoder_1_p2
  _7_Segment_Display #(.decimalPoint("false")) u_7_segment_display_1 ();  // open: g, f, a, b, e, d, c
endmodule

module Reg_Cache (
  input  ACERTO,
  input  A2,
  input  A1,
  input  Clock,
  input  [2:0] Reg_Rotulo,
  input  Reset,
  output [2:0] Rotulo_Guardado,
  output Valido_Indice
);

  wire decoder_1_out0, decoder_1_out1, decoder_1_out2, decoder_1_out3, not_1_out, Reg_Val_0_q, Reg_Val_1_q,
       Reg_Val_2_q, Reg_Val_3_q, undriven, undriven_2;
  wire [2:0] Reg_Rotulo_0_q, Reg_Rotulo_1_q, Reg_Rotulo_2_q, Reg_Rotulo_3_q;

  not not_1 (not_1_out, ACERTO);
  Decoder #(.select(2)) decoder_1 (
    .out0(decoder_1_out0), .out1(decoder_1_out1), .out2(decoder_1_out2), .out3(decoder_1_out3),
    .sel({A1, A2}), .en(not_1_out));
  Register #(.width(3)) Reg_Rotulo_0 (
    .D(Reg_Rotulo), .en(decoder_1_out0), .clk(Clock), .Q(Reg_Rotulo_0_q), .clr(undriven));
  Register #(.width(1)) Reg_Val_0 (.D(1'b1), .en(decoder_1_out0), .clk(Clock), .Q(Reg_Val_0_q), .clr(Reset));
  Register #(.width(3)) Reg_Rotulo_1 (
    .D(Reg_Rotulo), .en(decoder_1_out1), .clk(Clock), .Q(Reg_Rotulo_1_q), .clr(undriven_2));
  Register #(.width(1)) Reg_Val_1 (.D(1'b1), .en(decoder_1_out1), .clk(Clock), .Q(Reg_Val_1_q), .clr(Reset));
  Register #(.width(3)) Reg_Rotulo_2 (
    .D(Reg_Rotulo), .en(decoder_1_out2), .clk(Clock), .Q(Reg_Rotulo_2_q));  // open: clr
  Register #(.width(1)) Reg_Val_2 (.D(1'b1), .en(decoder_1_out2), .clk(Clock), .Q(Reg_Val_2_q), .clr(Reset));
  Register #(.width(3)) Reg_Rotulo_3 (
    .D(Reg_Rotulo), .en(decoder_1_out3), .clk(Clock), .Q(Reg_Rotulo_3_q));  // open: clr
  Register #(.width(1)) Reg_Val_3 (.D(1'b1), .en(decoder_1_out3), .clk(Clock), .Q(Reg_Val_3_q), .clr(Reset));
  Multiplexer #(.select(2), .width(3)) multiplexer_1 (
    .in0(Reg_Rotulo_0_q), .in1(Reg_Rotulo_1_q), .in2(Reg_Rotulo_2_q), .in3(Reg_Rotulo_3_q),
    .out(Rotulo_Guardado), .sel({A1, A2}));
  Multiplexer #(.select(2)) multiplexer_2 (
    .in0(Reg_Val_0_q), .in1(Reg_Val_1_q), .in2(Reg_Val_2_q), .in3(Reg_Val_3_q), .out(Valido_Indice),
    .sel({A1, A2}));
endmodule
